# Fritzing sketch Diagram (1) (saved by Fritzing 0.9.2b)
breadboards: 1

parts:
  LED = Red LED - 5mm [package="5 mm [THT]"]
  Resistor = Resistor [resistance=220 package=THT]
  PushButton = Pushbutton [package="[THT]"]
  Resistor_2 = Resistor [resistance=10k package=THT]
  RGBLedAnode = RGB LED - (4 legs) [package="5 mm [THT]"]
  Resistor_3 = Resistor [resistance=220 package=THT]
  Resistor_4 = Resistor [resistance=100 package=THT]
  Resistor_5 = Resistor [resistance=100 package=THT]
  Servo = Basic Servo
  Servo_2 = Basic Servo
  L7805 = Voltage Regulator - 5V [package="TO220 [THT]"]
  CapacitorCeramic = Ceramic Capacitor [capacitance=1uF package="200 mil [THT, multilayer]"]
  CapacitorElectro = Electrolytic Capacitor [capacitance=100nF package="200 mil [THT, electrolytic]"]
  ArduinoUno = Arduino Uno (Rev3) - ICSP

nets:
  N1: LED.cathode, Resistor.Pin_1
  N2: LED.anode, ArduinoUno.D3_PWM
  GND: Resistor.Pin_0, Resistor_2.Pin_1, Servo.gnd, Servo_2.gnd, L7805.GND, CapacitorCeramic.1, CapacitorElectro.-, ArduinoUno.GND
  N3: PushButton.Pin_1, PushButton.Pin_2, Resistor_2.Pin_0, ArduinoUno.D7
  VCC: PushButton.Pin_3, PushButton.Pin_4, RGBLedAnode.common_anode, Servo.vcc, Servo_2.vcc, L7805.output_voltage, CapacitorElectro.+
  N4: RGBLedAnode.red_cathode, Resistor_3.Pin_0
  N5: RGBLedAnode.green_cathode, Resistor_4.Pin_0
  N6: RGBLedAnode.blue_cathode, Resistor_5.Pin_0
  N7: Resistor_3.Pin_1, ArduinoUno.D9_PWM
  N8: Resistor_4.Pin_1, ArduinoUno.D6_PWM
  N9: Resistor_5.Pin_1, ArduinoUno.D5_PWM
  N10: Servo.pulse, ArduinoUno.D2
  N11: Servo_2.pulse, ArduinoUno.D4
  N12: L7805.input_voltage, CapacitorCeramic.0, ArduinoUno.VIN

custom parts:
  Basic Servo: A generic servo.
